# Fritzing sketch capDriverCircuit (saved by Fritzing 0.9.3b)
breadboards: 1

parts:
  TPIC6C594 = tpic6c596 [chip_label=TPIC6C596 package="DIP (Dual Inline) [THT]"]
  R1 = Resistor [tolerance=±5% resistance=33 package="0805 [SMD]"]
  R1_2 = Resistor [tolerance=±5% resistance=33 package="0805 [SMD]"]
  R1_3 = Resistor [tolerance=±5% resistance=33 package="0805 [SMD]"]
  R1_4 = Resistor [tolerance=±5% resistance=33 package="0805 [SMD]"]
  R1_5 = Resistor [tolerance=±5% resistance=33 package="0805 [SMD]"]
  R1_6 = Resistor [tolerance=±5% resistance=33 package="0805 [SMD]"]
  R1_7 = Resistor [tolerance=±5% resistance=33 package="0805 [SMD]"]
  ones_digit = 7 Segment Display
  Arduino_Nano_R4 = Arduino Nano (Rev3.0)
  7805 = Voltage Regulator [package=to220-igo]
  9–12V_in_center_+ = Power Jack [package=power_jack_pth]
  J8 = Screw terminal - 2 pins [package=THT]
  J9 = Screw terminal - 2 pins [package=THT]
  J10 = Screw terminal - 2 pins [package=THT]
  J11 = Screw terminal - 2 pins [package=THT]
  J12 = Screw terminal - 2 pins [package=THT]
  J13 = Screw terminal - 2 pins [package=THT]
  J14 = Screw terminal - 2 pins [package=THT]
  RJ45_jack1 = RJ45 Jack [package=rj45-8]
  SN75HVD3082EP1 = IC, DIP package, 8 pins [chip_label=IC]
  R4 = Resistor [tolerance=±5% resistance=220 package=THT]
  RX1 = LED - 5mm [color="Green (570nm)" package="5 mm [THT]"]
  TX1 = LED - 5mm [color="Red (633nm)" package="5 mm [THT]"]
  R5 = Resistor [tolerance=±5% resistance=1k package=THT]
  R6 = Resistor [tolerance=±5% resistance=1k package=THT]
  TPIC6C594_2 = tpic6c596 [chip_label=TPIC6C596 package="DIP (Dual Inline) [THT]"]
  R7 = Resistor [tolerance=±5% resistance=33 package="0805 [SMD]"]
  R8 = Resistor [tolerance=±5% resistance=33 package="0805 [SMD]"]
  R9 = Resistor [tolerance=±5% resistance=33 package="0805 [SMD]"]
  R10 = Resistor [tolerance=±5% resistance=33 package="0805 [SMD]"]
  R11 = Resistor [tolerance=±5% resistance=33 package="0805 [SMD]"]
  R1_8 = Resistor [tolerance=±5% resistance=33 package="0805 [SMD]"]
  R1_9 = Resistor [tolerance=±5% resistance=33 package="0805 [SMD]"]
  tens_digit = 7 Segment Display
  TPIC6C594_3 = tpic6c596 [chip_label=TPIC6C596 package="DIP (Dual Inline) [THT]"]
  R14 = Resistor [tolerance=±5% resistance=33 package="0805 [SMD]"]
  R15 = Resistor [tolerance=±5% resistance=33 package="0805 [SMD]"]
  R16 = Resistor [tolerance=±5% resistance=33 package="0805 [SMD]"]
  R17 = Resistor [tolerance=±5% resistance=33 package="0805 [SMD]"]
  R18 = Resistor [tolerance=±5% resistance=33 package="0805 [SMD]"]
  R1_10 = Resistor [tolerance=±5% resistance=33 package="0805 [SMD]"]
  R1_11 = Resistor [tolerance=±5% resistance=33 package="0805 [SMD]"]
  hundreds_digit = 7 Segment Display
  C1 = Ceramic Capacitor [capacitance=100nF package="100 mil [THT, multilayer]"]
  C1_2 = Ceramic Capacitor [capacitance=100nF package="100 mil [THT, multilayer]"]
  C1_3 = Ceramic Capacitor [capacitance=100nF package="100 mil [THT, multilayer]"]
  7805_2 = Voltage Regulator [package=78xxl]
  C3 = Tantalum Capacitor [package="100 mil [THT, tantalum]"]
  LED1 = smd LED [color="Red (633nm)" current=50mA package="1206 [SMD]"]
  LED2 = smd LED [color="Red (633nm)" current=50mA package="1206 [SMD]"]
  LED3 = smd LED [color="Red (633nm)" current=50mA package="1206 [SMD]"]
  LED4 = smd LED [color="Red (633nm)" current=50mA package="1206 [SMD]"]
  LED5 = smd LED [color="Red (633nm)" current=50mA package="1206 [SMD]"]
  LED6 = smd LED [color="Red (633nm)" current=50mA package="1206 [SMD]"]
  LED7 = smd LED [color="Red (633nm)" current=50mA package="1206 [SMD]"]
  LED8 = smd LED [color="Red (633nm)" current=50mA package="1206 [SMD]"]
  LED9 = smd LED [color="Red (633nm)" current=50mA package="1206 [SMD]"]
  LED11 = smd LED [color="Red (633nm)" current=50mA package="1206 [SMD]"]
  LED12 = smd LED [color="Red (633nm)" current=50mA package="1206 [SMD]"]
  LED13 = smd LED [color="Red (633nm)" current=50mA package="1206 [SMD]"]
  LED14 = smd LED [color="Red (633nm)" current=50mA package="1206 [SMD]"]
  LED15 = smd LED [color="Red (633nm)" current=50mA package="1206 [SMD]"]
  LED16 = smd LED [color="Red (633nm)" current=50mA package="1206 [SMD]"]
  LED17 = smd LED [color="Red (633nm)" current=50mA package="1206 [SMD]"]
  LED18 = smd LED [color="Red (633nm)" current=50mA package="1206 [SMD]"]
  LED19 = smd LED [color="Red (633nm)" current=50mA package="1206 [SMD]"]
  LED20 = smd LED [color="Red (633nm)" current=50mA package="1206 [SMD]"]
  LED21 = smd LED [color="Red (633nm)" current=50mA package="1206 [SMD]"]
  LED22 = smd LED [color="Red (633nm)" current=50mA package="1206 [SMD]"]
  LED23 = smd LED [color="Red (633nm)" current=50mA package="1206 [SMD]"]
  LED24 = smd LED [color="Red (633nm)" current=50mA package="1206 [SMD]"]
  LED25 = smd LED [color="Red (633nm)" current=50mA package="1206 [SMD]"]
  LED26 = smd LED [color="Red (633nm)" current=50mA package="1206 [SMD]"]
  LED27 = smd LED [color="Red (633nm)" current=50mA package="1206 [SMD]"]
  LED28 = smd LED [color="Red (633nm)" current=50mA package="1206 [SMD]"]
  LED29 = smd LED [color="Red (633nm)" current=50mA package="1206 [SMD]"]
  LED30 = smd LED [color="Red (633nm)" current=50mA package="1206 [SMD]"]
  LED31 = smd LED [color="Red (633nm)" current=50mA package="1206 [SMD]"]
  LED32 = smd LED [color="Red (633nm)" current=50mA package="1206 [SMD]"]
  LED33 = smd LED [color="Red (633nm)" current=50mA package="1206 [SMD]"]
  LED34 = smd LED [color="Red (633nm)" current=50mA package="1206 [SMD]"]
  LED35 = smd LED [color="Red (633nm)" current=50mA package="1206 [SMD]"]
  LED36 = smd LED [color="Red (633nm)" current=50mA package="1206 [SMD]"]
  LED37 = smd LED [color="Red (633nm)" current=50mA package="1206 [SMD]"]
  LED38 = smd LED [color="Red (633nm)" current=50mA package="1206 [SMD]"]
  LED39 = smd LED [color="Red (633nm)" current=50mA package="1206 [SMD]"]
  LED40 = smd LED [color="Red (633nm)" current=50mA package="1206 [SMD]"]
  LED41 = smd LED [color="Red (633nm)" current=50mA package="1206 [SMD]"]
  LED42 = smd LED [color="Red (633nm)" current=50mA package="1206 [SMD]"]
  LED43 = smd LED [color="Red (633nm)" current=50mA package="1206 [SMD]"]
  LED44 = smd LED [color="Red (633nm)" current=50mA package="1206 [SMD]"]
  LED45 = smd LED [color="Red (633nm)" current=50mA package="1206 [SMD]"]
  LED46 = smd LED [color="Red (633nm)" current=50mA package="1206 [SMD]"]
  LED47 = smd LED [color="Red (633nm)" current=50mA package="1206 [SMD]"]
  LED48 = smd LED [color="Red (633nm)" current=50mA package="1206 [SMD]"]
  LED49 = smd LED [color="Red (633nm)" current=50mA package="1206 [SMD]"]
  LED50 = smd LED [color="Red (633nm)" current=50mA package="1206 [SMD]"]
  LED51 = smd LED [color="Red (633nm)" current=50mA package="1206 [SMD]"]
  LED52 = smd LED [color="Red (633nm)" current=50mA package="1206 [SMD]"]
  LED53 = smd LED [color="Red (633nm)" current=50mA package="1206 [SMD]"]
  LED54 = smd LED [color="Red (633nm)" current=50mA package="1206 [SMD]"]
  LED55 = smd LED [color="Red (633nm)" current=50mA package="1206 [SMD]"]
  LED56 = smd LED [color="Red (633nm)" current=50mA package="1206 [SMD]"]
  LED57 = smd LED [color="Red (633nm)" current=50mA package="1206 [SMD]"]
  LED58 = smd LED [color="Red (633nm)" current=50mA package="1206 [SMD]"]
  LED59 = smd LED [color="Red (633nm)" current=50mA package="1206 [SMD]"]
  LED60 = smd LED [color="Red (633nm)" current=50mA package="1206 [SMD]"]
  LED61 = smd LED [color="Red (633nm)" current=50mA package="1206 [SMD]"]

nets:
  logic 5V: TPIC6C594.Vcc, TPIC6C594.CLR, TPIC6C594_2.Vcc, TPIC6C594_2.CLR, TPIC6C594_3.Vcc, TPIC6C594_3.CLR, C1.0, C1_2.0, C1_3.0, 7805_2.OUT
  N1: TPIC6C594.SER_IN, Arduino_Nano_R4.D11/MOSI, J13.pin2
  N2: TPIC6C594.DRAIN0, R1_4.Pin_1
  N3: TPIC6C594.DRAIN1, R1_5.Pin_1
  N4: TPIC6C594.DRAIN2, R1_6.Pin_1
  N5: TPIC6C594.DRAIN3, R1_7.Pin_1
  GND: TPIC6C594.G, TPIC6C594.GND, Arduino_Nano_R4.GND, 7805.GND, 9–12V_in_center_+.GND, RJ45_jack1.4, RJ45_jack1.5, SN75HVD3082EP1.pin5, TPIC6C594_2.G, TPIC6C594_2.GND, TPIC6C594_3.G, TPIC6C594_3.GND, C1.1, C1_2.1, C1_3.1, 7805_2.GND, C3.-
  N6: TPIC6C594.SER_OUT, TPIC6C594_2.SER_IN
  RCK: TPIC6C594.RCK, Arduino_Nano_R4.D13/SCK, J14.pin1, TPIC6C594_2.RCK, TPIC6C594_3.RCK
  N7: TPIC6C594.DRAIN4, R1_3.Pin_0
  N8: TPIC6C594.DRAIN5, R1.Pin_0
  N9: TPIC6C594.DRAIN6, R1_2.Pin_0
  SRCK: TPIC6C594.SRCK, Arduino_Nano_R4.D12/MISO, J13.pin1, TPIC6C594_2.SRCK, TPIC6C594_3.SRCK
  N10: R1.Pin_1, ones_digit.Segment_C
  N11: R1_2.Pin_1, ones_digit.Segment_B
  N12: R1_3.Pin_1, ones_digit.Segment_D
  N13: R1_4.Pin_0, ones_digit.Segment_A
  N14: R1_5.Pin_0, ones_digit.Segment_F
  N15: R1_6.Pin_0, ones_digit.Segment_G
  N16: R1_7.Pin_0, ones_digit.Segment_E
  31V: ones_digit.common_anode, tens_digit.common_anode, hundreds_digit.common_anode
  N17: Arduino_Nano_R4.D2, J9.pin1
  N18: Arduino_Nano_R4.D3, J9.pin2
  N19: Arduino_Nano_R4.D4, J8.pin1
  N20: Arduino_Nano_R4.D5, J8.pin2
  N21: Arduino_Nano_R4.D7, SN75HVD3082EP1.pin2, SN75HVD3082EP1.pin3
  N22: Arduino_Nano_R4.D8, SN75HVD3082EP1.pin1, TX1.cathode
  N23: Arduino_Nano_R4.D9, SN75HVD3082EP1.pin4, RX1.cathode
  N24: Arduino_Nano_R4.D10, J14.pin2
  N25: Arduino_Nano_R4.5V, 7805.OUT, R5.Pin_1, R6.Pin_1
  N26: Arduino_Nano_R4.A7, J10.pin1
  N27: Arduino_Nano_R4.A6, J10.pin2
  N28: Arduino_Nano_R4.A5, J11.pin1
  N29: Arduino_Nano_R4.A4, J11.pin2
  N30: Arduino_Nano_R4.A3, J12.pin1
  N31: Arduino_Nano_R4.A2, J12.pin2
  12V (DC transformer): 7805.IN, 9–12V_in_center_+.PWR, 7805_2.IN, C3.+
  N32: RJ45_jack1.7, SN75HVD3082EP1.pin7, R4.Pin_1
  N33: RJ45_jack1.8, SN75HVD3082EP1.pin6, R4.Pin_0
  N34: RX1.anode, R5.Pin_0
  N35: TX1.anode, R6.Pin_0
  N36: TPIC6C594_2.DRAIN0, R1_8.Pin_1
  N37: TPIC6C594_2.DRAIN1, R8.Pin_1
  N38: TPIC6C594_2.DRAIN2, R9.Pin_1
  N39: TPIC6C594_2.DRAIN3, R11.Pin_1
  N40: TPIC6C594_2.SER_OUT, TPIC6C594_3.SER_IN
  N41: TPIC6C594_2.DRAIN4, R10.Pin_0
  N42: TPIC6C594_2.DRAIN5, R7.Pin_0
  N43: TPIC6C594_2.DRAIN6, R1_9.Pin_0
  N44: R7.Pin_1, tens_digit.Segment_C
  N45: R8.Pin_0, tens_digit.Segment_F
  N46: R9.Pin_0, tens_digit.Segment_G
  N47: R10.Pin_1, tens_digit.Segment_D
  N48: R11.Pin_0, tens_digit.Segment_E
  N49: R1_8.Pin_0, tens_digit.Segment_A
  N50: R1_9.Pin_1, tens_digit.Segment_B
  N51: TPIC6C594_3.DRAIN0, R1_10.Pin_1
  N52: TPIC6C594_3.DRAIN1, R15.Pin_1
  N53: TPIC6C594_3.DRAIN2, R16.Pin_1
  N54: TPIC6C594_3.DRAIN3, R18.Pin_1
  N55: TPIC6C594_3.DRAIN4, R17.Pin_0
  N56: TPIC6C594_3.DRAIN5, R14.Pin_0
  N57: TPIC6C594_3.DRAIN6, R1_11.Pin_0
  N58: R14.Pin_1, hundreds_digit.Segment_C
  N59: R15.Pin_0, hundreds_digit.Segment_F
  N60: R16.Pin_0, hundreds_digit.Segment_G
  N61: R17.Pin_1, hundreds_digit.Segment_D
  N62: R18.Pin_0, hundreds_digit.Segment_E
  N63: R1_10.Pin_0, hundreds_digit.Segment_A
  N64: R1_11.Pin_1, hundreds_digit.Segment_B
  N65: LED1.cathode, LED2.anode
  N66: LED1.anode, LED17.anode, LED32.anode, LED40.anode
  N67: LED2.cathode, LED3.anode
  N68: LED3.cathode, LED4.anode
  N69: LED4.cathode, LED5.anode
  N70: LED5.cathode, LED8.anode
  N71: LED6.cathode, LED9.anode
  N72: LED6.anode, LED7.cathode
  N73: LED7.anode, LED8.cathode
  N74: LED9.cathode, LED13.anode
  N75: LED11.cathode, LED15.anode
  N76: LED11.anode, LED12.cathode
  N77: LED12.anode, LED13.cathode
  N78: LED14.cathode, LED16.anode
  N79: LED14.anode, LED15.cathode
  N80: LED16.cathode, LED19.cathode, LED60.cathode, LED61.cathode
  N81: LED17.cathode, LED25.anode
  N82: LED18.cathode, LED24.anode
  N83: LED18.anode, LED22.cathode
  N84: LED19.anode, LED26.cathode
  N85: LED20.cathode, LED26.anode
  N86: LED20.anode, LED31.cathode
  N87: LED21.cathode, LED29.anode
  N88: LED21.anode, LED25.cathode
  N89: LED22.anode, LED29.cathode
  N90: LED23.cathode, LED28.anode
  N91: LED23.anode, LED30.cathode
  N92: LED24.cathode, LED30.anode
  N93: LED27.cathode, LED31.anode
  N94: LED27.anode, LED28.cathode
  N95: LED32.cathode, LED52.anode
  N96: LED33.cathode, LED49.anode
  N97: LED33.anode, LED51.cathode
  N98: LED34.cathode, LED51.anode
  N99: LED34.anode, LED40.cathode
  N100: LED35.cathode, LED36.anode
  N101: LED35.anode, LED54.cathode
  N102: LED36.cathode, LED45.anode
  N103: LED37.cathode, LED38.anode
  N104: LED37.anode, LED59.cathode
  N105: LED38.cathode, LED46.anode
  N106: LED39.cathode, LED54.anode
  N107: LED39.anode, LED41.cathode
  N108: LED41.anode, LED49.cathode
  N109: LED42.cathode, LED53.anode
  N110: LED42.anode, LED52.cathode
  N111: LED43.cathode, LED57.anode
  N112: LED43.anode, LED45.cathode
  N113: LED44.cathode, LED48.anode
  N114: LED44.anode, LED50.cathode
  N115: LED46.cathode, LED60.anode
  N116: LED47.cathode, LED58.anode
  N117: LED47.anode, LED48.cathode
  N118: LED50.anode, LED53.cathode
  N119: LED55.cathode, LED59.anode
  N120: LED55.anode, LED58.cathode
  N121: LED56.cathode, LED61.anode
  N122: LED56.anode, LED57.cathode

notes:
  Capitalism Works For Me, This is the capPodium PCB, 0.2
  Capitalism Works For Me, This is the protoboard-mounted circuit, 0.1
  Capitalism Works For Me, BL-SE1200B-11UHR LED segment detail
  R1 = 33Ω
  Detail of BL-SE1200B-11UHR LED segment internal wiring; each LED die has a V_F of 2–2.2V and draws 5–20mA. Therefore each segment has a V_F of 30–33V and draws 20–80mA.

custom parts:
  tpic6c596: serial-to-parallel chip with 8 switched current sinking outputs
  Tantalum Capacitor: Tantalum capacitor. Plus lead is usually marked and is usually the longer lead.
